# Fritzing sketch puzzlebox (saved by Fritzing 0.9.2b)
breadboards: 1

parts:
  atmega328p-pu = atmega328 [package=dip]
  Crystal = Crystal [frequency="16 Mhz" package=THT]
  C1 = Ceramic Capacitor [capacitance=22pF voltage=6.3V package="100 mil [THT, multilayer]"]
  C2 = Ceramic Capacitor [capacitance=22pF voltage=6.3V package="100 mil [THT, multilayer]"]
  5v = Power plug
  Trellis = Adafruit Trellis

nets:
  VCC: atmega328p-pu.VCC, atmega328p-pu.AVCC, 5v.VCC, Trellis.5V
  GND: atmega328p-pu.GND, C1.0, C2.0, 5v.GND, Trellis.GND
  N1: atmega328p-pu.XLAT1, Crystal.pin_0, C2.1
  N2: atmega328p-pu.XLAT2, Crystal.pin_1, C1.1
  N3: atmega328p-pu.A2, Trellis.INT
  N4: atmega328p-pu.A4, Trellis.SDA
  N5: atmega328p-pu.A5, Trellis.SCL
